# Fritzing sketch mailboxdetection (saved by Fritzing 0.9.3b)

parts:
  U1 = Mystery Part - 2 pins [chip_label=? package=THT]
  Part1 = Arduino Pro Mini (5V)
  WeMos_D1_Mini1 = WeMos D1 Mini
  VCC1 = Battery
  R1 = Resistor [tolerance=±5% resistance=10k package=THT]
  Part2 = GY-VL53L0XV2 Laser Ranger Module
  R2 = Resistor [tolerance=±5% resistance=10k package=THT]

nets:
  3V3: U1.VOUT+, WeMos_D1_Mini1.3V3, Part2.VCC
  N1: U1.VOUT-, WeMos_D1_Mini1.G, Part2.GND, R2.Pin_0
  N2: U1.VIN+, Part1.VCC, VCC1.+
  N3: U1.VIN-, Part1.GND, VCC1.-, R1.Pin_0
  N4: Part1.D6, R1.Pin_1
  N5: Part1.D5, WeMos_D1_Mini1.RST
  N6: Part1.D2, WeMos_D1_Mini1.D3
  N7: WeMos_D1_Mini1.D1, Part2.SCL
  N8: WeMos_D1_Mini1.D2, Part2.SDA
  N9: WeMos_D1_Mini1.D8, Part2.XSHUT, R2.Pin_1

custom parts:
  Mystery Part - 2 pins: A dummy, proxy, ersatz, stand-in part for whatever you want. With 2 pins on a 100 mil inline pin header footprint.
  GY-VL53L0XV2 Laser Ranger Module: The GY-VL53L0XV2 is based on the VL53L0X from ST Microelectronics, a time-of-flight ranging system integrated into a compact module.
